# Fritzing sketch 110519018 wk11 (saved by Fritzing 0.9.3b)
breadboards: 1

parts:
  元件1 = Arduino Uno (Rev3) - ICSP
  LED2 = smd LED [color="Orange (620nm)" package="0603 [SMD]"]
  LED3 = smd LED [color="Red (633nm)" package="0603 [SMD]"]
  LED4 = smd LED [color="Green (560nm)" package="0603 [SMD]"]

nets:
  N1: 元件1.ICSP_MISO, 元件1.D12/MISO, LED2.cathode
  N2: 元件1.ICSP_MOSI, 元件1.D11_PWM/MOSI, LED4.anode
  N3: 元件1.D13/SCK, LED3.anode
  N4: 元件1.GND, LED2.anode, LED3.cathode, LED4.cathode
